// Logisim project IT012.R11.2_Lab02_25520174.circ as structural Verilog
module FA (
  input  A,
  input  B,
  input  Cin,
  output S,
  output Cout
);

  wire and_1_out, and_2_out, xor_1_out;

  xor xor_1 (xor_1_out, A, B);
  and and_1 (and_1_out, A, B);
  xor xor_2 (S, xor_1_out, Cin);
  and and_2 (and_2_out, xor_1_out, Cin);
  or or_1 (Cout, and_1_out, and_2_out);
endmodule

module ADDSUB4 (
  input  [3:0] A,
  input  [3:0] B,
  input  SUB,
  output X3,
  output Y3,
  output S3,
  output [3:0] out_7,
  output N,
  output C1,
  output C2,
  output C3,
  output C,
  output Z
);

  wire xor_1_out, xor_2_out, xor_3_out;

  FA fa_1 (.A(A[0]), .B(xor_1_out), .Cin(SUB), .S(out_7[0]), .Cout(C1));
  xor xor_1 (xor_1_out, B[0], SUB);
  FA fa_2 (.A(A[1]), .B(xor_2_out), .Cin(C1), .S(out_7[1]), .Cout(C2));
  xor xor_2 (xor_2_out, B[1], SUB);
  FA fa_3 (.A(A[2]), .B(xor_3_out), .Cin(C2), .S(out_7[2]), .Cout(C3));
  xor xor_3 (xor_3_out, B[2], SUB);
  FA fa_4 (.A(A[3]), .B(Y3), .Cin(C3), .S(N), .Cout(C));
  xor xor_4 (Y3, B[3], SUB);
  nor nor_1 (Z, N, out_7[2], out_7[1], out_7[0]);

  assign out_7[3] = N;
  assign S3 = N;
  assign X3 = A[3];
endmodule

module ALU8 (
  input  [2:0] OP,
  input  [7:0] A,
  input  [7:0] B,
  output [7:0] R,
  output Z
);

  wire [7:0] adder_1_out, adder_2_out, and_1_out, multiplexer_1_out, multiplexer_2_out, nand_1_out, or_1_out,
       subtractor_1_out, subtractor_2_out, xor_1_out;

  Adder adder_1 (.a(A), .b(B), .out(adder_1_out));  // open: cin, cout
  Adder adder_2 (.a(A), .b(8'h1), .out(adder_2_out));  // open: cin, cout
  Subtractor subtractor_1 (.a(A), .b(B), .out(subtractor_1_out));  // open: bin, bout
  Subtractor subtractor_2 (.a(A), .b(8'h1), .out(subtractor_2_out));  // open: bin, bout
  assign and_1_out = A & B;  // AND_Gate and_1, 8 bits wide
  assign or_1_out = A | B;  // OR_Gate or_1, 8 bits wide
  assign nand_1_out = ~A;  // NAND_Gate nand_1, 8 bits wide NAND_Gate
  assign xor_1_out = A ^ B;  // XOR_Gate xor_1, 8 bits wide
  Multiplexer #(.select(2), .width(8)) multiplexer_1 (
    .in0(adder_1_out), .in1(adder_2_out), .in2(subtractor_1_out), .in3(subtractor_2_out),
    .out(multiplexer_1_out), .sel(OP[1:0]));  // open: en
  Multiplexer #(.select(2), .width(8)) multiplexer_2 (
    .in0(and_1_out), .in1(or_1_out), .in2(nand_1_out), .in3(xor_1_out), .out(multiplexer_2_out), .sel(OP[1:0]));  // open: en
  Multiplexer #(.width(8)) multiplexer_3 (
    .in0(multiplexer_1_out), .in1(multiplexer_2_out), .out(R), .sel(OP[2]));  // open: en
  nor nor_1 (Z, R[7], R[6], R[5], R[4], R[3], R[2], R[1], R[0]);
endmodule

module LT (
  input  [2:0] in_1,
  input  [7:0] A,
  input  [7:0] B,
  output out_4,
  output LT,
  output [7:0] R
);

  wire and_1_out, and_2_out, and_3_out, not_1_out;

  ALU8 alu8_1 (.OP(in_1), .A(A), .B(B), .Z(out_4), .R(R));
  not not_1 (not_1_out, B[7]);
  and and_1 (and_1_out, A[7], not_1_out);
  and and_2 (and_2_out, A[7], R[7]);
  and and_3 (and_3_out, R[7], not_1_out);
  or or_1 (LT, and_1_out, and_2_out, and_3_out);
endmodule

module DLATCH (
  input  D,
  input  E,
  output Q
);

  Multiplexer multiplexer_1 (.in0(Q), .in1(D), .out(Q), .sel(E));  // open: en
endmodule

module TN3 (
  input  CLK,
  input  D,
  input  D_2,
  input  CLK_2,
  output Q1,
  output out_6,
  output out_7,
  output Q2
);

  wire d_ff_3_q, dlatch_3_q;

  DLATCH dlatch_1 (.D(D), .E(CLK), .Q(Q1));
  D_Flip_Flop d_ff_1 (.clk(CLK), .D(D), .Q(Q2));  // open: Qn, preset, en, reset
  DLATCH dlatch_2 (.D(dlatch_3_q), .E(CLK_2), .Q(out_6));
  DLATCH dlatch_3 (.D(D_2), .E(CLK_2), .Q(dlatch_3_q));
  D_Flip_Flop d_ff_2 (.clk(CLK_2), .D(d_ff_3_q), .Q(out_7));  // open: Qn, preset, en, reset
  D_Flip_Flop d_ff_3 (.clk(CLK_2), .D(D_2), .Q(d_ff_3_q));  // open: Qn, preset, en, reset
endmodule

module DFF_MS (
  input  D,
  input  CLK,
  output Q3
);

  wire dlatch_1_q, not_1_out;

  not not_1 (not_1_out, CLK);
  DLATCH dlatch_1 (.D(D), .E(not_1_out), .Q(dlatch_1_q));
  DLATCH dlatch_2 (.D(dlatch_1_q), .E(CLK), .Q(Q3));
endmodule

module REGFILE (
  input  CLK,
  input  [1:0] RA,
  input  WE,
  input  [1:0] RD,
  input  [7:0] DIN,
  input  [1:0] RB,
  output [7:0] QA,
  output [7:0] QB
);

  wire decoder_1_out0, decoder_1_out1, decoder_1_out2, decoder_1_out3;
  wire [7:0] register_1_q, register_2_q, register_3_q, register_4_q;

  Decoder #(.select(2)) decoder_1 (
    .out0(decoder_1_out0), .out1(decoder_1_out1), .out2(decoder_1_out2), .out3(decoder_1_out3), .sel(RD),
    .en(WE));
  Register register_1 (.D(DIN), .en(decoder_1_out0), .Q(register_1_q), .clk(CLK));  // open: clr
  Register register_2 (.D(DIN), .en(decoder_1_out1), .Q(register_2_q), .clk(CLK));  // open: clr
  Register register_3 (.D(DIN), .en(decoder_1_out2), .Q(register_3_q), .clk(CLK));  // open: clr
  Register register_4 (.D(DIN), .en(decoder_1_out3), .Q(register_4_q), .clk(CLK));  // open: clr
  Multiplexer #(.select(2), .width(8)) multiplexer_1 (
    .in0(register_1_q), .in1(register_2_q), .in2(register_3_q), .in3(register_4_q), .out(QA), .sel(RA));  // open: en
  Multiplexer #(.select(2), .width(8)) multiplexer_2 (
    .in0(register_1_q), .in1(register_2_q), .in2(register_3_q), .in3(register_4_q), .out(QB), .sel(RB));  // open: en
endmodule

module DATAPATH (
);

  wire [7:0] alu8_1_r;

  REGFILE regfile_1 (.DIN(alu8_1_r));  // open: CLK, RA, WE, RD, RB, QA, QB
  ALU8 alu8_1 (.R(alu8_1_r));  // open: OP, A, B, Z
  Multiplexer #(.width(8)) multiplexer_1 ();  // open: in0, in1, out, sel, en
endmodule
